# Fritzing sketch Focuser (saved by Fritzing 0.9.3b)

parts:
  Part1 = ESP-WROOM-32 [ESP-32S] Module [part_number=ESP-WROOM-32]
  SM1 = 28BYJ-48 Stepper Motor [part_number=28BYJ-48]
  Driver1 = 28BYJ-48 Driver Module [part_number=ULN2003 package=THT]
  Part2 = Arduino Joystick Shield
  Part3 = ESP-WROOM-32 [ESP-32S] Module [part_number=ESP-WROOM-32]
  Driver2 = 28BYJ-48 Driver Module [part_number=ULN2003 package=THT]
  SM2 = 28BYJ-48 Stepper Motor [part_number=28BYJ-48]
  RE1 = KY-040 Rotary encoder [package="Breakout board"]
  Driver3 = 28BYJ-48 Driver Module [part_number=ULN2003 package=THT]
  SM3 = 28BYJ-48 Stepper Motor [part_number=28BYJ-48]
  Part4 = Arduino Ethernet Shield (Rev3)
  RE2 = KY-040 Rotary encoder [package="Breakout board"]

nets:
  N1: Part1.IO34, Part2.HORIZONTAL
  N2: Part1.IO35, Part2.VERTICAL
  N3: Part1.IO33, Part2.SEL
  N4: Part1.IO26, Part2.D3
  N5: Part1.IO14, Part2.D4
  N6: Part1.IO13, Part2.D5
  N7: Part1.IO5, Driver1.IN4
  N8: Part1.IO19, Driver1.IN3
  N9: Part1.IO21, Driver1.IN2
  N10: Part1.IO23, Driver1.IN1
  N11: SM1.blue-pin, Driver1.blue-pin
  N12: SM1.pink-pin, Driver1.pink-pin
  N13: SM1.yellow-pin, Driver1.yellow-pin
  N14: SM1.orange-pin, Driver1.orange-pin
  N15: SM1.red-pin, Driver1.red-pin
  N16: Part3.IO34, RE1.CLK
  N17: Part3.IO32, RE1.DT
  N18: Part3.IO25, RE1.SW
  N19: Part3.IO5, Driver2.IN4
  N20: Part3.IO19, Driver2.IN3
  N21: Part3.IO21, Driver2.IN2
  N22: Part3.IO23, Driver2.IN1
  N23: Driver2.blue-pin, SM2.blue-pin
  N24: Driver2.pink-pin, SM2.pink-pin
  N25: Driver2.yellow-pin, SM2.yellow-pin
  N26: Driver2.orange-pin, SM2.orange-pin
  N27: Driver2.red-pin, SM2.red-pin
  N28: Driver3.IN1, Part4.PWM_D9
  N29: Driver3.IN2, Part4.ETH_CS
  N30: Driver3.IN3, Part4.PWM_D11
  N31: Driver3.IN4, Part4.SPI/D12
  N32: Driver3.blue-pin, SM3.blue-pin
  N33: Driver3.pink-pin, SM3.pink-pin
  N34: Driver3.yellow-pin, SM3.yellow-pin
  N35: Driver3.orange-pin, SM3.orange-pin
  N36: Driver3.red-pin, SM3.red-pin
  N37: Part4.PWM_D3, RE2.CLK
  N38: Part4.SDCS, RE2.DT
  N39: Part4.PWM_D5, RE2.SW

custom parts:
  ESP-WROOM-32 [ESP-32S] Module: Espressif ESP-WROOM-32 WiFi/Bluetooth LE microcontroller module also known as the Ai-Thinker ESP-32S module with similar formfactor. The ESP32 is a microcontroller chip with WiFi and BLE capabilities. The chip is developed by Espressif and is the successor to the popular ESP8266 WiFi module.
  28BYJ-48 Stepper Motor: Unipolar Stepper Motor 28BYJ-48 Top coil - pink & orange Bottom coil - blue & yellow Common rail - red Connector pins: blue - pink - yellow - orange - red
  28BYJ-48 Driver Module: High-power ULN2003 Stepper Motor Driver Board Test Module For Arduino AVR SMD
  KY-040 Rotary encoder: KY-040 Rotary Encoder with switch on breakout borad from AZ Delivery
